# Fritzing sketch Circuit (saved by Fritzing 0.9.10b)

parts:
  ESP32-CAM = ESP32 - CAM
  M1 = Dagu DGServo 9g (End View) [part_number=RS001B]
  Y_Axis = Dagu DGServo 9g (End View) [part_number=RS001B]
  Part1 = Arduino Uno (Rev3) - ICSP
  Part2 = Bluetooth HC-05 Macho

nets:
  GND: ESP32-CAM.GND, M1.gnd, Y_Axis.gnd, Part1.GND, Part2.GND
  VCC: ESP32-CAM.5V, M1.vcc, Y_Axis.vcc, Part1.5V, Part2.VCC
  N1: M1.pulse, Part1.D10_PWM/SS
  N2: Y_Axis.pulse, Part1.D9_PWM
  N3: Part1.D0/RX, Part2.TXD
  N4: Part1.D1/TX, Part2.RXD

custom parts:
  ESP32 - CAM: The ESP32-CAM has a very competitive small-size camera module that can operate independently as a minimum system with a footprint of only 27*40.5*4.5mm and a deep sleep current of up to 6mA.
